// Logisim project shubham.circ as structural Verilog: 1 circuit, main circuit main
module main (
  input  D0,
  input  D1,
  input  D2,
  input  D3,
  input  D4,
  input  D5,
  input  D6,
  input  D7,
  input  D8,
  input  D9,
  input  D10,
  input  D11,
  input  D12,
  input  D13,
  input  D14,
  input  D15,
  input  S1,
  input  S2,
  input  S3,
  input  S4,
  output out_21
);

  wire A0_out, A7_out, A8_out, A9_out;

  // NOT_Gate not_1 has open pins: in=S1, out=open
  // NOT_Gate not_2 has open pins: in=S2, out=open
  // NOT_Gate not_3 has open pins: in=S3, out=open
  // NOT_Gate not_4 has open pins: in=S4, out=open
  buf A0 (A0_out, D0);  // AND_Gate
  buf A1 (A0_out, D1);  // AND_Gate
  buf A2 (A0_out, D2);  // AND_Gate
  buf A3 (A0_out, D3);  // AND_Gate
  buf A4 (A0_out, D4);  // AND_Gate
  buf A5 (A0_out, D5);  // AND_Gate
  buf A6 (A0_out, D6);  // AND_Gate
  buf A7 (A7_out, D7);  // AND_Gate
  buf A8 (A8_out, D8);  // AND_Gate
  buf A9 (A9_out, D9);  // AND_Gate
  buf A10 (A9_out, D10);  // AND_Gate
  buf A11 (A9_out, D11);  // AND_Gate
  buf A12 (A9_out, D12);  // AND_Gate
  // AND_Gate A13 has open pins: in0=D13, out=open
  buf A14 (A9_out, D14);  // AND_Gate
  buf A15 (A9_out, D15);  // AND_Gate
  or or_1 (out_21, A0_out, A0_out, A0_out, A0_out, A0_out, A0_out, A0_out, A7_out, A8_out, A9_out, A9_out, A9_out, A9_out, A9_out, A9_out, A9_out);
endmodule
